# Fritzing sketch Xentrino-2WD-Buffer-2-Teensy 3.2 (saved by Fritzing 0.9.3b)

parts:
  Teensy_3_4 = Teensy 3.0 [part_number="Freescale ARM MK20DX128"]
  IC3 = PICAXE-20M [package=THT]
  Part3 = Monster Moto Shield
  GY4 = MPU-6050 Board GY-521 [form="♀ (female)" package=THT]  # not connected
  BAT2 = BC9VPC [package=bc9vpc]
  J3 = Screw terminal - 2 pins [package=THT]
  U2 = Voltage Regulator [package=v-reg_dpack]  # not connected
  JP8 = Header 6 [package=molex-1x6_lock]  # not connected
  JP9 = Header 6 [package=molex-1x6_lock]
  JP10 = Header 6 [package=molex-1x6_lock]
  JP11 = Header 6 [package=molex-1x6_lock]

nets:
  N1: Teensy_3_4.17, JP9.6
  N2: Teensy_3_4.16, JP9.5
  N3: Teensy_3_4.15, JP9.4
  N4: Teensy_3_4.14, JP9.3
  N5: Teensy_3_4.13, JP9.2
  N6: Teensy_3_4.GND, IC3.Serial_Out
  N7: Teensy_3_4.0, IC3.Out_0_/_Infraout
  N8: Teensy_3_4.1, IC3.Out_1
  N9: Teensy_3_4.2, IC3.Out_2
  N10: Teensy_3_4.3, IC3.Out_3
  N11: Teensy_3_4.4, IC3.Out_4
  N12: Teensy_3_4.5, IC3.Out_5
  N13: Teensy_3_4.6, IC3.Out_6
  N14: Teensy_3_4.7, IC3.Out_7
  N15: IC3.Serial_In, Part3.INB2_-_D9
  N16: IC3.In_7_/_ADC_7, Part3.INB1_-_D8
  N17: IC3.In_6, Part3.INA1_-_D7
  N18: IC3.In_5, Part3.PWM2_-_D6
  N19: IC3.In_4, Part3.PWM1_-_D5
  N20: IC3.In_3_/_ADC_3, Part3.INA2_-_D4
  N21: Part3.OUTA1, JP10.2
  N22: Part3.OUTB1, JP10.1
  N23: Part3.OUTA2, JP11.5
  N24: Part3.OUTB2, JP11.6
  N25: Part3.GND, Part3.GND_-_GND@0, Part3.GND_-_GND@2
  N26: BAT2.V+, J3.pin1
  N27: BAT2.V-, J3.pin2

custom parts:
  MPU-6050 Board GY-521: Acelerometro y Giroscopio MPU-6050 Board GY-521
