# Fritzing sketch Xentrino-2WD-Teensy 3.2 (saved by Fritzing 0.9.2b)

parts:
  Part1 = Monster Moto Shield
  Teensy_3_1 = Teensy 3.0 [part_number="Freescale ARM MK20DX128"]
  GY2 = MPU-6050 Board GY-521 [form="♀ (female)" package=THT]
  C1 = Capacitor Polarized [package=cpol-radial-10uf-25v]  # not connected
  C2 = Capacitor Polarized [package=cpol-radial-10uf-25v]  # not connected
  U1 = Voltage Regulator - 5V [package="TO220 [THT]"]
  M1 = DC Motor
  M2 = DC Motor
  Part2 = Lilypad Battery Connect  # not connected
  JP1 = Header 6 [package=molex-1x6_lock]
  JP2 = Header 6 [package=molex-1x6_lock]
  JP3 = Header 2 [package=screwterminal-3.5mm-2_lock]
  JP6 = Header 2 [package=screwterminal-3.5mm-2_lock]
  JP7 = Header 6 [package=molex-1x6_lock]

nets:
  N1: Part1.OUTA1, M2.pin_1
  N2: Part1.OUTB1, M2.pin_2
  N3: Part1.OUTA2, M1.pin_1
  N4: Part1.OUTB2, M1.pin_2
  N5: Part1.3.3V, Teensy_3_1.3.3V#2
  5V: Part1.5V, Teensy_3_1.Vin, U1.output_voltage
  N6: Part1.EN1_-_A0, Teensy_3_1.7
  N7: Part1.EN2_-_A1, Teensy_3_1.8
  N8: Part1.INA2_-_D4, Teensy_3_1.5
  N9: Part1.PWM1_-_D5, Teensy_3_1.4
  N10: Part1.PWM2_-_D6, Teensy_3_1.3
  N11: Part1.INA1_-_D7, Teensy_3_1.2
  N12: Part1.INB2_-_D9, Teensy_3_1.1
  N13: Part1.GND_-_GND@0, Part1.GND_-_GND@1, Part1.GND_-_GND@2
  N14: Teensy_3_1.23, JP6.2
  N15: Teensy_3_1.22, JP6.1
  N16: Teensy_3_1.21, JP3.2
  N17: Teensy_3_1.20, JP1.1
  N18: Teensy_3_1.19, GY2.pin3
  N19: Teensy_3_1.18, GY2.pin4
  N20: Teensy_3_1.17, JP1.2
  N21: Teensy_3_1.16, JP1.3
  N22: Teensy_3_1.15, JP1.4
  N23: Teensy_3_1.14, JP1.5
  N24: Teensy_3_1.13, JP1.6
  N25: Teensy_3_1.6, JP3.1
  N26: Teensy_3_1.9, JP2.6
  N27: Teensy_3_1.10, JP2.5
  N28: Teensy_3_1.11, JP2.4
  N29: Teensy_3_1.12, JP2.3
  N30: Teensy_3_1.3.3V#36, JP7.4
  N31: Teensy_3_1.VBat, JP7.5
  N32: Teensy_3_1.Program, JP7.2
  N33: Teensy_3_1.GND#39, JP7.3
  N34: Teensy_3_1.RST, JP7.1

custom parts:
  MPU-6050 Board GY-521: Acelerometro y Giroscopio MPU-6050 Board GY-521
