# Fritzing sketch Xentrino-4WD-Buffer-2-Teensy 3.2 (saved by Fritzing 0.9.3b)

parts:
  IC3 = PICAXE-20M [package=THT]
  Part3 = Monster Moto Shield
  GY4 = MPU-6050 Board GY-521 [form="♀ (female)" package=THT]  # not connected
  BAT2 = BC9VPC [package=bc9vpc]  # not connected
  J3 = Screw terminal - 2 pins [package=THT]  # not connected
  U2 = Voltage Regulator [package=v-reg_dpack]  # not connected
  JP10 = Header 6 [package=molex-1x6_lock]
  JP11 = Header 6 [package=molex-1x6_lock]
  Part4 = Monster Moto Shield
  IC4 = PICAXE-20M [package=THT]
  Teensy_3_4 = Teensy 3.0 [part_number="Freescale ARM MK20DX128"]
  JP12 = Header 6 [package=molex-1x6_lock]
  JP13 = Header 6 [package=molex-1x6_lock]
  JP14 = Header 6 [package=molex-1x6_lock]

nets:
  N1: IC3.Serial_In, Part3.INB2_-_D9
  N2: IC3.In_7_/_ADC_7, Part3.INB1_-_D8
  N3: IC3.In_6, Part3.INA1_-_D7
  N4: IC3.In_5, Part3.PWM2_-_D6
  N5: IC3.In_4, Part3.PWM1_-_D5
  N6: IC3.In_3_/_ADC_3, Part3.INA2_-_D4
  N7: IC3.Out_5, Teensy_3_4.5
  N8: IC3.Out_4, Teensy_3_4.4
  N9: IC3.Out_3, Teensy_3_4.3
  N10: IC3.Out_2, Teensy_3_4.2
  N11: IC3.Out_1, Teensy_3_4.1
  N12: IC3.Out_0_/_Infraout, Teensy_3_4.0
  N13: IC3.Serial_Out, Teensy_3_4.GND
  N14: Part3.OUTA1, JP10.2
  N15: Part3.OUTB1, JP10.1
  N16: Part3.OUTA2, JP11.5
  N17: Part3.OUTB2, JP11.6
  N18: Part3.GND, Part3.GND_-_GND@0, Part3.GND_-_GND@2
  N19: Part4.OUTA1, JP12.2
  N20: Part4.OUTB1, JP12.1
  N21: Part4.OUTA2, JP13.5
  N22: Part4.OUTB2, JP13.6
  N23: Part4.INA2_-_D4, IC4.In_3_/_ADC_3
  N24: Part4.PWM1_-_D5, IC4.In_4
  N25: Part4.PWM2_-_D6, IC4.In_5
  N26: Part4.INA1_-_D7, IC4.In_6
  N27: Part4.INB1_-_D8, IC4.In_7_/_ADC_7
  N28: Part4.INB2_-_D9, IC4.Serial_In
  N29: Teensy_3_4.13, JP14.1
  N30: Teensy_3_4.12, JP14.5
  N31: Teensy_3_4.3.3V#36, JP14.3
  N32: Teensy_3_4.VBat, JP14.4
  N33: Teensy_3_4.RST, JP14.2

custom parts:
  MPU-6050 Board GY-521: Acelerometro y Giroscopio MPU-6050 Board GY-521
